# Fritzing sketch washer (saved by Fritzing 0.9.6b)
circuit board: 8.46667cm x 5.64444cm
breadboards: 1

parts:
  U1 = NodeMCU V1.0
  Part1 = Adafruit LIS3DH [part_number="Adafruit #2809"]
  Part2 = Adafruit LIS3DH [part_number="Adafruit #2809"]

nets:
  N1: U1.D1, Part1.SCL, Part2.SCL
  N2: U1.D2, Part1.SDA, Part2.SDA
  VIN: U1.3V3, Part1.VIN, Part2.VIN, Part2.SDO
  GND: U1.GND, Part1.GND, Part2.GND

custom parts:
  NodeMCU V1.0: ESP8266 based NodeMCU
  Adafruit LIS3DH: The LIS3DH is a very popular low power triple-axis accelerometer. It's low-cost, but has just about every 'extra' you'd want in an accelerometer: Three axis sensing, 10-bit precision ±2g/±4g/±8g/±16g selectable scaling Both I2C (2 possible addresses) and SPI interface options Interrupt output Multiple data rate options 1 Hz to 5Khz As low as 2uA current draw (just the chip itself, not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
